# Fritzing sketch VolvoPedalCommander (saved by Fritzing 0.9.3b)

parts:
  Onderdeel1 = Arduino Nano (Rev3.0)
  Q1 = NPN-Transistor [package="TO92 [THT]"]
  Onderdeel2 = Adafruit MCP4725 Breakout Board - 12-Bit DAC [part_number="Adafruit #935"]
  R1 = Resistor [tolerance=±5% resistance=10k package="0402 [SMD]"]
  R2 = Resistor [tolerance=±5% resistance=10k package="0402 [SMD]"]

nets:
  N1: Onderdeel1.D2, R1.Pin_0
  N2: Onderdeel1.D8, R2.Pin_1
  N3: Onderdeel1.A5, Onderdeel2.SCL
  N4: Onderdeel1.A4, Onderdeel2.SDA
  N5: Q1.B, R2.Pin_0

notes:
  1 2 3 4 5 6
  6 5 4 3 2 1
  Pedal (input)
  Car (output)

custom parts:
  Adafruit MCP4725 Breakout Board - 12-Bit DAC: Your microcontroller probably has an ADC (analog -> digital converter) but does it have a DAC (digital -> analog converter)??? Now it can! This breakout board features the easy-to-use MCP4725 12-bit DAC. Control it via I2C and send it the value you want it to output, and the VOUT pin will have it. Great for audio / analog projects, such as when you can't use PWM but need a sine wave or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
